// Logisim project gpu.circ as structural Verilog: 1 circuit, main circuit main
module main (
);

  wire button_1_out, clock_1_out;
  wire [6:0] rgb_video_1_p4, rgb_video_1_p5;

  Button button_1 (.out(button_1_out));
  Clock clock_1 (.out(clock_1_out));
  // RGB_Video rgb_video_1: pin names not known; wires that end beside it: button_1_out, clock_1_out, 1'b1, rgb_video_1_p4, rgb_video_1_p5, {24{1'b1}}
  Counter #(.max('h3fff), .width(14)) counter_1 (
    .Q({rgb_video_1_p5, rgb_video_1_p4}), .clk(clock_1_out), .clr(button_1_out));  // open: load, D, count, carry
endmodule
